// Logisim project PC.circ as structural Verilog: 1 circuit, main circuit MAIN
module MAIN (
);

  wire and_1_out, and_2_out, and_3_out, and_4_out, and_5_out, and_6_out, and_7_out, and_8_out, and_9_out,
       and_10_out, and_11_out, and_12_out, and_13_out, and_14_out, and_15_out, and_16_out, and_17_out,
       and_18_out, and_19_out, and_20_out, and_21_out, and_22_out, and_23_out, and_24_out, and_25_out,
       and_26_out, and_27_out, and_28_out, and_29_out, and_30_out, and_31_out, and_32_out, and_33_out,
       and_34_out, and_35_out, and_36_out, and_37_out, and_38_out, and_39_out, and_40_out, and_41_out,
       and_42_out, and_43_out, and_44_out, and_45_out, and_46_out, and_47_out, CLK, nand_1_out, nand_2_out,
       nand_3_out, nand_4_out, nand_5_out, nand_6_out, nand_7_out, nand_8_out, nand_9_out, nand_10_out,
       nand_11_out, nand_12_out, nand_13_out, nand_14_out, nand_15_out, nand_16_out, nand_17_out,
       nand_18_out, nand_19_out, nand_20_out, nand_21_out, nand_22_out, nand_23_out, nand_24_out,
       nand_25_out, nand_26_out, nand_27_out, nand_28_out, nand_29_out, nand_30_out, nand_31_out,
       nand_32_out, nand_33_out, nand_34_out, nand_35_out, nand_36_out, nand_37_out, nand_38_out,
       nand_39_out, nand_40_out, nand_41_out, nand_42_out, nand_43_out, nand_44_out, nand_45_out,
       nand_46_out, nand_47_out, nand_48_out, nand_49_out, nand_50_out, nand_51_out, nand_52_out,
       nand_53_out, nand_54_out, nand_55_out, nand_56_out, nand_57_out, nand_58_out, nand_59_out,
       nand_60_out, nand_61_out, nand_62_out, nand_63_out, nand_64_out, not_1_out, not_2_out, not_3_out,
       not_4_out, not_5_out, not_6_out, not_7_out, not_8_out, not_9_out, not_10_out, not_11_out, not_12_out,
       not_13_out, not_14_out, not_15_out, not_16_out, PC_RE, PC_WE, undriven, undriven_2, undriven_3,
       undriven_4, undriven_5, undriven_6, undriven_7, undriven_8, undriven_9, undriven_10, undriven_11,
       undriven_12, undriven_13, undriven_14, undriven_15, undriven_16, xor_1_out, xor_2_out, xor_3_out,
       xor_4_out, xor_5_out, xor_6_out, xor_7_out, xor_8_out, xor_9_out, xor_10_out, xor_11_out, xor_12_out,
       xor_13_out, xor_14_out, xor_15_out, xor_16_out;

  not not_1 (not_1_out, and_1_out);
  not not_2 (not_2_out, and_3_out);
  not not_3 (not_3_out, and_5_out);
  not not_4 (not_4_out, and_7_out);
  not not_5 (not_5_out, and_9_out);
  not not_6 (not_6_out, and_11_out);
  not not_7 (not_7_out, and_13_out);
  not not_8 (not_8_out, and_15_out);
  not not_9 (not_9_out, and_17_out);
  not not_10 (not_10_out, and_19_out);
  not not_11 (not_11_out, and_21_out);
  not not_12 (not_12_out, and_23_out);
  not not_13 (not_13_out, and_25_out);
  not not_14 (not_14_out, and_27_out);
  not not_15 (not_15_out, and_29_out);
  not not_16 (not_16_out, and_31_out);
  nand nand_1 (nand_1_out, and_1_out, CLK);
  nand nand_2 (nand_2_out, CLK, not_1_out);
  nand nand_3 (nand_3_out, and_3_out, CLK);
  nand nand_4 (nand_4_out, CLK, not_2_out);
  nand nand_5 (nand_5_out, and_5_out, CLK);
  nand nand_6 (nand_6_out, CLK, not_3_out);
  nand nand_7 (nand_7_out, and_7_out, CLK);
  nand nand_8 (nand_8_out, CLK, not_4_out);
  nand nand_9 (nand_9_out, and_9_out, CLK);
  nand nand_10 (nand_10_out, CLK, not_5_out);
  nand nand_11 (nand_11_out, and_11_out, CLK);
  nand nand_12 (nand_12_out, CLK, not_6_out);
  nand nand_13 (nand_13_out, and_13_out, CLK);
  nand nand_14 (nand_14_out, CLK, not_7_out);
  nand nand_15 (nand_15_out, and_15_out, CLK);
  nand nand_16 (nand_16_out, CLK, not_8_out);
  nand nand_17 (nand_17_out, and_17_out, CLK);
  nand nand_18 (nand_18_out, CLK, not_9_out);
  nand nand_19 (nand_19_out, and_19_out, CLK);
  nand nand_20 (nand_20_out, CLK, not_10_out);
  nand nand_21 (nand_21_out, and_21_out, CLK);
  nand nand_22 (nand_22_out, CLK, not_11_out);
  nand nand_23 (nand_23_out, and_23_out, CLK);
  nand nand_24 (nand_24_out, CLK, not_12_out);
  nand nand_25 (nand_25_out, and_25_out, CLK);
  nand nand_26 (nand_26_out, CLK, not_13_out);
  nand nand_27 (nand_27_out, and_27_out, CLK);
  nand nand_28 (nand_28_out, CLK, not_14_out);
  nand nand_29 (nand_29_out, and_29_out, CLK);
  nand nand_30 (nand_30_out, CLK, not_15_out);
  nand nand_31 (nand_31_out, and_31_out, CLK);
  nand nand_32 (nand_32_out, CLK, not_16_out);
  nand nand_33 (nand_33_out, nand_1_out, nand_34_out);
  nand nand_34 (nand_34_out, nand_33_out, nand_2_out);
  nand nand_35 (nand_35_out, nand_3_out, nand_36_out);
  nand nand_36 (nand_36_out, nand_35_out, nand_4_out);
  nand nand_37 (nand_37_out, nand_5_out, nand_38_out);
  nand nand_38 (nand_38_out, nand_37_out, nand_6_out);
  nand nand_39 (nand_39_out, nand_7_out, nand_40_out);
  nand nand_40 (nand_40_out, nand_39_out, nand_8_out);
  nand nand_41 (nand_41_out, nand_9_out, nand_42_out);
  nand nand_42 (nand_42_out, nand_41_out, nand_10_out);
  nand nand_43 (nand_43_out, nand_11_out, nand_44_out);
  nand nand_44 (nand_44_out, nand_43_out, nand_12_out);
  nand nand_45 (nand_45_out, nand_13_out, nand_46_out);
  nand nand_46 (nand_46_out, nand_45_out, nand_14_out);
  nand nand_47 (nand_47_out, nand_15_out, nand_48_out);
  nand nand_48 (nand_48_out, nand_47_out, nand_16_out);
  nand nand_49 (nand_49_out, nand_17_out, nand_50_out);
  nand nand_50 (nand_50_out, nand_49_out, nand_18_out);
  nand nand_51 (nand_51_out, nand_19_out, nand_52_out);
  nand nand_52 (nand_52_out, nand_51_out, nand_20_out);
  nand nand_53 (nand_53_out, nand_21_out, nand_54_out);
  nand nand_54 (nand_54_out, nand_53_out, nand_22_out);
  nand nand_55 (nand_55_out, nand_23_out, nand_56_out);
  nand nand_56 (nand_56_out, nand_55_out, nand_24_out);
  nand nand_57 (nand_57_out, nand_25_out, nand_58_out);
  nand nand_58 (nand_58_out, nand_57_out, nand_26_out);
  nand nand_59 (nand_59_out, nand_27_out, nand_60_out);
  nand nand_60 (nand_60_out, nand_59_out, nand_28_out);
  nand nand_61 (nand_61_out, nand_29_out, nand_62_out);
  nand nand_62 (nand_62_out, nand_61_out, nand_30_out);
  nand nand_63 (nand_63_out, nand_31_out, nand_64_out);
  nand nand_64 (nand_64_out, nand_63_out, nand_32_out);
  and and_1 (and_1_out, PC_WE, and_2_out);
  and and_2 (and_2_out, nand_33_out, PC_RE);
  and and_3 (and_3_out, PC_WE, and_4_out);
  and and_4 (and_4_out, nand_35_out, PC_RE);
  and and_5 (and_5_out, PC_WE, and_6_out);
  and and_6 (and_6_out, nand_37_out, PC_RE);
  and and_7 (and_7_out, PC_WE, and_8_out);
  and and_8 (and_8_out, nand_39_out, PC_RE);
  and and_9 (and_9_out, PC_WE, and_10_out);
  and and_10 (and_10_out, nand_41_out, PC_RE);
  and and_11 (and_11_out, PC_WE, and_12_out);
  and and_12 (and_12_out, nand_43_out, PC_RE);
  and and_13 (and_13_out, PC_WE, and_14_out);
  and and_14 (and_14_out, nand_45_out, PC_RE);
  and and_15 (and_15_out, PC_WE, and_16_out);
  and and_16 (and_16_out, nand_47_out, PC_RE);
  and and_17 (and_17_out, PC_WE, and_18_out);
  and and_18 (and_18_out, nand_49_out, PC_RE);
  and and_19 (and_19_out, PC_WE, and_20_out);
  and and_20 (and_20_out, nand_51_out, PC_RE);
  and and_21 (and_21_out, PC_WE, and_22_out);
  and and_22 (and_22_out, nand_53_out, PC_RE);
  and and_23 (and_23_out, PC_WE, and_24_out);
  and and_24 (and_24_out, nand_55_out, PC_RE);
  and and_25 (and_25_out, PC_WE, and_26_out);
  and and_26 (and_26_out, nand_57_out, PC_RE);
  and and_27 (and_27_out, PC_WE, and_28_out);
  and and_28 (and_28_out, nand_59_out, PC_RE);
  and and_29 (and_29_out, PC_WE, and_30_out);
  and and_30 (and_30_out, nand_61_out, PC_RE);
  and and_31 (and_31_out, PC_WE, and_32_out);
  and and_32 (and_32_out, nand_63_out, PC_RE);
  and and_33 (and_33_out, 1'b1, undriven);
  and and_34 (and_34_out, and_33_out, undriven_2);
  and and_35 (and_35_out, and_34_out, undriven_3);
  and and_36 (and_36_out, and_35_out, undriven_4);
  and and_37 (and_37_out, and_36_out, undriven_5);
  and and_38 (and_38_out, and_37_out, undriven_6);
  and and_39 (and_39_out, and_38_out, undriven_7);
  and and_40 (and_40_out, and_39_out, undriven_8);
  and and_41 (and_41_out, and_40_out, undriven_9);
  and and_42 (and_42_out, and_41_out, undriven_10);
  and and_43 (and_43_out, and_42_out, undriven_11);
  and and_44 (and_44_out, and_43_out, undriven_12);
  and and_45 (and_45_out, and_44_out, undriven_13);
  and and_46 (and_46_out, and_45_out, undriven_14);
  and and_47 (and_47_out, and_46_out, undriven_15);
  // AND_Gate and_48 has open pins: in0=and_47_out, in1=undriven_16, out=open
  xor xor_1 (xor_1_out, 1'b1, undriven);
  xor xor_2 (xor_2_out, and_33_out, undriven_2);
  xor xor_3 (xor_3_out, and_34_out, undriven_3);
  xor xor_4 (xor_4_out, and_35_out, undriven_4);
  xor xor_5 (xor_5_out, and_36_out, undriven_5);
  xor xor_6 (xor_6_out, and_37_out, undriven_6);
  xor xor_7 (xor_7_out, and_38_out, undriven_7);
  xor xor_8 (xor_8_out, and_39_out, undriven_8);
  xor xor_9 (xor_9_out, and_40_out, undriven_9);
  xor xor_10 (xor_10_out, and_41_out, undriven_10);
  xor xor_11 (xor_11_out, and_42_out, undriven_11);
  xor xor_12 (xor_12_out, and_43_out, undriven_12);
  xor xor_13 (xor_13_out, and_44_out, undriven_13);
  xor xor_14 (xor_14_out, and_45_out, undriven_14);
  xor xor_15 (xor_15_out, and_46_out, undriven_15);
  xor xor_16 (xor_16_out, and_47_out, undriven_16);
  DipSwitch dipswitch_1 (.sw1(PC_WE), .sw2(PC_RE));  // open: sw3, sw4, sw5, sw6, sw7, sw8
  Button button_1 (.out(CLK));
endmodule
